# Fritzing sketch sketch (saved by Fritzing 0.8.0b)
breadboards: 1

parts:
  Arduino1 = Arduino
  RH1 = Humidity Sensor
  LED1 = LED - 5mm [color="Red (633nm)" package="5 mm [THT]"]
  LED2 = LED - 5mm [color="Blue (525nm)" package="5 mm [THT]"]
  R2 = Resistor [tolerance=±5% resistance=1k package=THT]
  R3 = Resistor [tolerance=±5% resistance=1k package=THT]
  T1 = LM35 Temperature Sensor [package="TO92 [THT]"]
  R4 = Photocell (LDR) [package=THT]
  R5 = Resistor [tolerance=±5% resistance=10k package=THT]

nets:
  N1: Arduino1.D13, R3.Pin_1
  N2: Arduino1.D12, R2.Pin_1
  +5V: Arduino1.+5V, RH1.Vcc, T1.+Vs, R4.pin_0
  GND: Arduino1.GND, RH1.GND, LED1.cathode, LED2.cathode, T1.GND, R4.pin_1, R5.Pin_0
  N3: Arduino1.A0, RH1.Analog_data-signal
  N4: Arduino1.A2, T1.Vout
  N5: LED1.anode, R3.Pin_0
  N6: LED2.anode, R2.Pin_0

custom parts:
  Humidity Sensor: Analog/digital relative humidity sensor.
